# Fritzing sketch Meteostation_schematic (saved by Fritzing 0.9.3b)

parts:
  U5 = NodeMCU V3.0
  J1 = DHT11 basic temperature-humidity sensor [form="♂ (male)" package=THT]
  Part1 = BMP085
  S1 = Reed switch [package=THT]  # not connected
  R1 = Resistor [tolerance=±5% resistance=5k package=THT]
  LED1 = smd LED [color="Red (633nm)" package="0603 [SMD]"]

nets:
  N1: U5.D0, U5.D3, U5.3V3, J1.OUT
  N2: U5.D1, Part1.SCL, Part1.CLR
  N3: U5.D2, Part1.SDA
  N4: U5.D7, LED1.anode
  VCC: J1.VCC, Part1.3V3
  N5: Part1.GND, R1.Pin_1

custom parts:
  NodeMCU V3.0: NodeMcu V3 Lua WIFI Development Board
  DHT11 basic temperature-humidity sensor: The DHT11 is a basic, ultra low-cost digital temperature and humidity sensor. It uses a capacitive humidity sensor and a thermistor to measure the surrounding air, and spits out a digital signal on the data pin (no analog input pins needed). Its fairly simple to use, but requires careful timing to grab data. The only real downside of this sensor is you can only get new data from it once every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
  BMP085: Pressure sensor
